# Fritzing sketch vwcdcemu_attiny85 (saved by Fritzing 0.9.3b)
perfboards: 1

parts:
  U1 = Voltage Regulator - 5V [package="TO220 [THT]"]
  J1 = female pin header, 5 pins [form="♀ (female)"]
  C1 = Electrolytic Capacitor [capacitance=1µF package="100 mil [THT, electrolytic]"]
  R1 = Resistor [tolerance=±5% resistance=3.3k package=THT]
  R2 = Resistor [tolerance=±5% resistance=3.3k package=THT]
  R3 = Resistor [tolerance=±5% resistance=3.3k package=THT]
  R4 = Resistor [tolerance=±5% resistance=220 package=THT]
  LED1 = LED - 5mm [color="Red (633nm)" package="5 mm [THT]"]

nets:
  N1: U1.input_voltage, J1.pin1
  N2: U1.GND, J1.pin5, C1.-, R4.Pin_0
  N3: U1.output_voltage, C1.+, LED1.anode
  N4: J1.pin2, R1.Pin_0
  N5: J1.pin3, R2.Pin_0
  N6: J1.pin4, R3.Pin_0
  N7: R4.Pin_1, LED1.cathode

notes:
  GND
